# Fritzing sketch invernadero_auto (saved by Fritzing 0.9.3b)

parts:
  JP1 = Header 2 [package=molex-1x2_lock]
  M1 = RioRand LM2596
  JP2 = Header 2 [package=molex-1x2_lock]
  Componente1 = Arduino Nano (Rev3.0)
  DHT1 = DHT11 Humitidy and Temperature Sensor
  U1 = 4-Channel 5v Relay Shield [package=relay-4ch5v10a]

nets:
  N1: JP1.1, M1.Pin_2
  N2: JP1.2, M1.Pin_1
  5V: M1.Pin_3, JP2.2, Componente1.5V, DHT1.VDD, U1.VCC
  GND: M1.Pin_4, JP2.1, Componente1.GND, DHT1.GND, U1.GND
  N3: Componente1.D2, DHT1.DATA
  N4: Componente1.D7, U1.IN4
  N5: Componente1.D8, U1.IN3
  N6: Componente1.D9, U1.IN2
  N7: Componente1.D10, U1.IN1

custom parts:
  DHT11 Humitidy and Temperature Sensor: DHT11 Humidity and Temperature Sensor
  4-Channel 5v Relay Shield: 4 Channel 5v Relay Shield w. 2x SPD-06VDC-SD-C
